# Fritzing sketch power cutter (saved by Fritzing 0.9.2b)
circuit board: 8.46667cm x 5.64444cm
breadboards: 1

parts:
  R1 = Resistor [tolerance=±5% resistance=2.2k package=THT]
  R2 = Resistor [tolerance=±5% resistance=2.2k package=THT]
  Q2 = npn-Powertransistor [part_number=BD139 package="TO220 [THT]"]
  RaspberryPi1 = Raspberry Pi Model B
  Q1 = NPN-Transistor [part_number=BC547 package="TO92 [THT]"]
  U2 = Voltage Regulator - 3.3V [part_number=LM7833 package="TO220 [THT]"]
  C3 = Electrolytic Capacitor [capacitance=0.1mF package="100 mil [THT, electrolytic]"]
  C4 = Electrolytic Capacitor [capacitance=0.1mF package="100 mil [THT, electrolytic]"]

nets:
  N1: R1.Pin_0, RaspberryPi1.5V, U2.input_voltage, C3.+
  N2: R1.Pin_1, Q2.base, Q1.C
  N3: R2.Pin_0, RaspberryPi1.#18
  N4: R2.Pin_1, Q1.B
  GND: Q2.collector, Q2.emitter, RaspberryPi1.GND, Q1.E, U2.GND, C3.-, C4.-
  +3.3V: U2.output_voltage, C4.+

custom parts:
  Raspberry Pi Model B: Raspberry Pi (Model B)
